// Logisim project PathFinder.circ as structural Verilog
module CPU (
  input  in_1,
  input  in_2,
  input  [7:0] PC,
  input  [7:0] in_4
);

  wire clk_out, controlunit_1_memread, controlunit_1_memtoreg, controlunit_1_memwrite, controlunit_1_regwrite;
  wire [1:0] controlunit_1_aluop;
  wire [2:0] multiplexer_1_out, rom_1_data, rom_1_data_2, rom_1_data_3, rom_1_data_4;
  wire [7:0] alu_1_result, bit_extender_1_out, memory_1_p5, multiplexer_2_out, multiplexer_3_out,
       registerfile_1_readdataa, registerfile_1_readdatab;
  wire [15:12] rom_1_data_5;

  Counter counter_1 (.clr(in_1), .load(in_2), .up(1'b1), .count(1'b1), .clk(clk_out), .D(in_4), .Q(PC));  // open: carry
  Clock clk (.out(clk_out));
  ROM #(.dataWidth(16)) rom_1 (.addr(PC), .data({rom_1_data_5, rom_1_data_4, rom_1_data_3, rom_1_data_2, rom_1_data}));
  assign bit_extender_1_out = {{5{rom_1_data[2]}}, rom_1_data};  // Bit_Extender bit_extender_1
  Multiplexer #(.width(3)) multiplexer_1 (
    .in0(rom_1_data_4), .in1(rom_1_data_4), .out(multiplexer_1_out), .sel(controlunit_1_memwrite));
  ControlUnit controlunit_1 (
    .Opcode(rom_1_data_5), .RegWrite(controlunit_1_regwrite), .MemtoReg(controlunit_1_memtoreg),
    .MemRead(controlunit_1_memread), .MemWrite(controlunit_1_memwrite), .ALUop(controlunit_1_aluop));  // open: Jump
  RegisterFile registerfile_1 (
    .Data(multiplexer_2_out), .clk(clk_out), .Enable(controlunit_1_regwrite), .WriteAtAddress(rom_1_data_4),
    .SelectReadA(rom_1_data_3), .SelectReadB(multiplexer_1_out), .ReadDataA(registerfile_1_readdataa),
    .ReadDataB(registerfile_1_readdatab));
  // Memory memory_1: pin names not known; wires that end beside it: clk_out, {rom_1_data_3, rom_1_data_2}, controlunit_1_memwrite, controlunit_1_memread, memory_1_p5
  Multiplexer #(.width(8)) multiplexer_2 (
    .in1(memory_1_p5), .out(multiplexer_2_out), .sel(controlunit_1_memtoreg));  // open: in0
  Multiplexer #(.width(8)) multiplexer_3 (
    .in0(registerfile_1_readdatab), .in1(bit_extender_1_out), .out(multiplexer_3_out));  // open: sel
  ALU alu_1 (.A(registerfile_1_readdataa), .B(multiplexer_3_out), .ALUop(controlunit_1_aluop), .Result(alu_1_result));

  // Notes on the sheet:
  //   contents of rom_1 (hex, n*v repeats v):
  //   4228
endmodule

module ControlUnit (
  input  [3:0] Opcode,
  output RegWrite,
  output MemtoReg,
  output MemRead,
  output MemWrite,
  output Jump,
  output [1:0] ALUop
);

  wire decoder_1_out0, decoder_1_out1, decoder_1_out2, decoder_1_out3;

  Decoder #(.select(4)) decoder_1 (
    .out0(decoder_1_out0), .out1(decoder_1_out1), .out2(decoder_1_out2), .out3(decoder_1_out3),
    .out4(MemRead), .out5(MemWrite), .out6(Jump), .sel(Opcode), .en(1'b1));  // open: out7, out8, out9, out10, out11, out12, out13, out14, out15
  or or_1 (RegWrite, decoder_1_out0, decoder_1_out1, decoder_1_out2, decoder_1_out3, MemRead);

  assign ALUop = Opcode[1:0];
  assign MemtoReg = MemRead;
endmodule

module ALU (
  input  [7:0] A,
  input  [7:0] B,
  input  [1:0] ALUop,
  output [7:0] Result
);

  wire [7:0] adder_1_out, and_1_out, or_1_out, subtractor_1_out;

  Adder adder_1 (.a(A), .b(B), .out(adder_1_out));  // open: cin, cout
  Subtractor subtractor_1 (.a(A), .b(B), .out(subtractor_1_out));  // open: bin, bout
  assign and_1_out = A & B;  // AND_Gate and_1, 8 bits wide
  assign or_1_out = A | B;  // OR_Gate or_1, 8 bits wide
  Multiplexer #(.select(2), .width(8)) multiplexer_1 (
    .in0(adder_1_out), .in1(subtractor_1_out), .in2(and_1_out), .in3(or_1_out), .out(Result), .sel(ALUop));
endmodule

module RegisterFile (
  input  [7:0] Data,
  input  clk,
  input  Enable,
  input  [2:0] WriteAtAddress,
  input  [2:0] SelectReadA,
  input  [2:0] SelectReadB,
  output [7:0] ReadDataA,
  output [7:0] ReadDataB
);

  wire decoder_1_out0, decoder_1_out1, decoder_1_out2, decoder_1_out3, decoder_1_out4, decoder_1_out5,
       decoder_1_out6, decoder_1_out7;
  wire [7:0] R0_q, R1_q, R2_q, R3_q, R4_q, R5_q, R6_q, R7_q;

  Decoder #(.select(3)) decoder_1 (
    .out0(decoder_1_out0), .out1(decoder_1_out1), .out2(decoder_1_out2), .out3(decoder_1_out3),
    .out4(decoder_1_out4), .out5(decoder_1_out5), .out6(decoder_1_out6), .out7(decoder_1_out7),
    .sel(WriteAtAddress), .en(Enable));
  Register R0 (.D(Data), .en(decoder_1_out0), .clk(clk), .Q(R0_q));  // open: clr
  Register R1 (.D(Data), .en(decoder_1_out1), .clk(clk), .Q(R1_q));  // open: clr
  Register R2 (.D(Data), .en(decoder_1_out2), .clk(clk), .Q(R2_q));  // open: clr
  Register R3 (.D(Data), .en(decoder_1_out3), .clk(clk), .Q(R3_q));  // open: clr
  Register R4 (.D(Data), .en(decoder_1_out4), .clk(clk), .Q(R4_q));  // open: clr
  Register R5 (.D(Data), .en(decoder_1_out5), .clk(clk), .Q(R5_q));  // open: clr
  Register R6 (.D(Data), .en(decoder_1_out6), .clk(clk), .Q(R6_q));  // open: clr
  Register R7 (.D(Data), .en(decoder_1_out7), .clk(clk), .Q(R7_q));  // open: clr
  Multiplexer #(.select(3), .width(8)) multiplexer_1 (
    .in0(R0_q), .in1(R1_q), .in2(R2_q), .in3(R3_q), .in4(R4_q), .in5(R5_q), .in6(R6_q), .in7(R7_q),
    .out(ReadDataA), .sel(SelectReadA));
  Multiplexer #(.select(3), .width(8)) multiplexer_2 (
    .in0(R0_q), .in1(R1_q), .in2(R2_q), .in3(R3_q), .in4(R4_q), .in5(R5_q), .in6(R6_q), .in7(R7_q),
    .out(ReadDataB), .sel(SelectReadB));
endmodule

module Memory (
  input  [5:0] Address,
  input  WriteEnable,
  input  ReadEnable,
  input  clk,
  input  [7:0] DataIn,
  output [7:0] DataOut
);

  RAM #(.addrWidth(6)) Memory (
    .addr(Address), .we(WriteEnable), .oe(ReadEnable), .clk(clk), .din(DataIn), .dout(DataOut));
endmodule
